# Fritzing sketch autolevel (saved by Fritzing 0.9.4)
circuit board: 10cm x 7cm
breadboards: 1

parts:
  DRV_1 = DRV 8825 Stepper Motor Carrier, High Current [part_number="DRV 8825"]
  DRV_2 = DRV 8825 Stepper Motor Carrier, High Current [part_number="DRV 8825"]
  Nano1 = Arduino Nano v2.3
  Componente1 = InvenSense MPU6050
  J1 = Screw terminal - 2 pins [package=THT]
  J2 = female pin header, 4 pins [form="♀ (female)"]
  J3 = female pin header, 4 pins [form="♀ (female)"]
  C1 = Electrolytic Capacitor [capacitance=0.1mF voltage=16V package="100 mil [THT, electrolytic]"]
  C2 = Electrolytic Capacitor [capacitance=0.1mF voltage=16V package="100 mil [THT, electrolytic]"]
  Componente2 = Bluetooth HC-05 Macho
  R1 = Resistor [tolerance=±5% resistance=220 package=THT]
  R2 = Resistor [tolerance=±5% resistance=220 package=THT]

nets:
  +5V: DRV_1.RESET, DRV_1.SLEEP, DRV_2.RESET, DRV_2.SLEEP, Nano1.+5V, Componente2.VCC
  N1: DRV_1.STEP, Nano1.D7
  N2: DRV_1.DIRECTION, Nano1.D6
  N3: DRV_1.VOLTAGE_ST/_MT, DRV_2.VOLTAGE_ST/_MT, Nano1.VIN, J1.pin1, C1.+, C2.+
  GND: DRV_1.GROUND_ST/_MT, DRV_1.GROUND_LOG, DRV_2.GROUND_ST/_MT, DRV_2.GROUND_LOG, Nano1.GND, Componente1.GND, J1.pin2, C1.-, C2.-, Componente2.GND, R2.Pin_1
  N4: DRV_1.OUT_2B, J3.pin4
  N5: DRV_1.OUT_2A, J3.pin3
  N6: DRV_1.OUT_1A, J3.pin2
  N7: DRV_1.OUT_1B, J3.pin1
  N8: DRV_2.STEP, Nano1.D5
  N9: DRV_2.DIRECTION, Nano1.D4
  N10: DRV_2.OUT_2B, J2.pin4
  N11: DRV_2.OUT_2A, J2.pin3
  N12: DRV_2.OUT_1A, J2.pin2
  N13: DRV_2.OUT_1B, J2.pin1
  N14: Nano1.D2, Componente1.INT
  N15: Nano1.D10, R1.Pin_0
  N16: Nano1.D11, Componente2.RXD
  3V3: Nano1.3V3, Componente1.VCC
  N17: Nano1.A5, Componente1.SCL
  N18: Nano1.A4, Componente1.SDA
  N19: Componente2.TXD, R1.Pin_1, R2.Pin_0
