# Fritzing sketch autolevel2 (saved by Fritzing 0.9.4)
circuit board: 10cm x 7cm
breadboards: 1

parts:
  DRV_1 = DRV 8825 Stepper Motor Carrier, High Current [part_number="DRV 8825"]
  DRV_2 = DRV 8825 Stepper Motor Carrier, High Current [part_number="DRV 8825"]
  Componente1 = InvenSense MPU6050
  J1 = Screw terminal - 2 pins [package=THT]
  J2 = female pin header, 4 pins [form="♀ (female)"]
  J3 = female pin header, 4 pins [form="♀ (female)"]
  C1 = Electrolytic Capacitor [capacitance=0.1mF voltage=16V package="100 mil [THT, electrolytic]"]
  C2 = Electrolytic Capacitor [capacitance=0.1mF voltage=16V package="100 mil [THT, electrolytic]"]
  Componente2 = Bluetooth HC-05 Macho
  R1 = Resistor [tolerance=±5% resistance=220 package=THT]
  R2 = Resistor [tolerance=±5% resistance=220 package=THT]
  Componente3 = Arduino Nano (Rev3.0)

nets:
  N1: DRV_1.ENABLE, DRV_2.ENABLE, Componente3.D12/MISO
  VCC: DRV_1.RESET, DRV_1.SLEEP, DRV_2.RESET, DRV_2.SLEEP, Componente1.VCC, Componente2.VCC, Componente3.5V
  N2: DRV_1.STEP, Componente3.D7
  N3: DRV_1.DIRECTION, Componente3.D6
  N4: DRV_1.VOLTAGE_ST/_MT, DRV_2.VOLTAGE_ST/_MT, J1.pin1, C1.+, C2.+, Componente3.VIN
  GND: DRV_1.GROUND_ST/_MT, DRV_1.GROUND_LOG, DRV_2.GROUND_ST/_MT, DRV_2.GROUND_LOG, Componente1.GND, J1.pin2, C1.-, C2.-, Componente2.GND, R2.Pin_1, Componente3.GND
  N5: DRV_1.OUT_2B, J3.pin4
  N6: DRV_1.OUT_2A, J3.pin3
  N7: DRV_1.OUT_1A, J3.pin2
  N8: DRV_1.OUT_1B, J3.pin1
  N9: DRV_2.STEP, Componente3.D5
  N10: DRV_2.DIRECTION, Componente3.D4
  N11: DRV_2.OUT_2B, J2.pin4
  N12: DRV_2.OUT_2A, J2.pin3
  N13: DRV_2.OUT_1A, J2.pin2
  N14: DRV_2.OUT_1B, J2.pin1
  N15: Componente1.SCL, Componente3.A5
  N16: Componente1.SDA, Componente3.A4
  N17: Componente1.INT, Componente3.D2
  N18: Componente2.TXD, R1.Pin_1, R2.Pin_0
  N19: Componente2.RXD, Componente3.D0/RX
  N20: R1.Pin_0, Componente3.D1/TX
